# Fritzing sketch circuit_diagram (saved by Fritzing 0.9.3b)

parts:
  R1 = Resistor [tolerance=±5% resistance=4.7k package=THT]
  Part1 = Arduino Nano (Rev3.0)
  Amperemeter1 = Amperemeter
  R2 = TRIMPOT [package=trim_pot_pth]
  DS1 = DS18B20 1-Wire Temperature Sensor [part_number=DS18B20]

nets:
  N1: R1.Pin_0, DS1.DQ
  5V: R1.Pin_1, Part1.5V, DS1.VDD
  GND: Part1.GND, DS1.GND
  N2: Part1.D10, R2.CW
  N3: Part1.D11/MOSI, Amperemeter1.Com
  N4: Amperemeter1.Positive, R2.WIPER

custom parts:
  Amperemeter: A Standard Multimeter in Current mode
